// Logisim project adder_subtractor_for_alu.circ as structural Verilog: 1 circuit, main circuit main
module main (
  input  \signal_från_avkodare ,
  input  b0,
  input  a0,
  input  b1,
  input  a1,
  input  b2,
  input  a2,
  input  b3,
  input  a3
);

  wire adder_1_cout, adder_1_out, adder_2_cout, adder_2_out, adder_3_cout, adder_3_out, adder_4_out,
       xor_1_out, xor_2_out, xor_3_out, xor_4_out;

  xor xor_1 (xor_1_out, b0, \signal_från_avkodare );
  xor xor_2 (xor_2_out, b1, \signal_från_avkodare );
  xor xor_3 (xor_3_out, b2, \signal_från_avkodare );
  xor xor_4 (xor_4_out, b3, \signal_från_avkodare );
  Adder #(.width(1)) adder_1 (
    .a(xor_1_out), .b(a0), .out(adder_1_out), .cin(\signal_från_avkodare ), .cout(adder_1_cout));
  Adder #(.width(1)) adder_2 (.a(xor_2_out), .b(a1), .out(adder_2_out), .cin(adder_1_cout), .cout(adder_2_cout));
  Adder #(.width(1)) adder_3 (.a(xor_3_out), .b(a2), .out(adder_3_out), .cin(adder_2_cout), .cout(adder_3_cout));
  Adder #(.width(1)) adder_4 (.a(xor_4_out), .b(a3), .out(adder_4_out), .cin(adder_3_cout));  // open: cout
  LED led_1 (.in(adder_1_out));
  LED led_2 (.in(adder_2_out));
  LED led_3 (.in(adder_3_out));
  LED led_4 (.in(adder_4_out));
endmodule
