// Logisim project logisim_alu.circ as structural Verilog: 1 circuit, main circuit main
module main (
);

  wire undriven_9;
  wire [2:0] undriven_8;
  wire [7:0] Register_1__RS1_q, Register_2__RS2_q;
  wire [31:0] adder_1_out, multiplexer_1_out, undriven, undriven_2, undriven_3, undriven_4, undriven_5,
       undriven_6, undriven_7;

  Register Register_2__RS2 (.Q(Register_2__RS2_q));  // open: D, en, clk, clr
  Register Register_1__RS1 (.Q(Register_1__RS1_q));  // open: D, en, clk, clr
  Adder adder_1 (.a(Register_1__RS1_q), .b(Register_2__RS2_q), .out(adder_1_out[7:0]));  // open: cin, cout
  Subtractor subtractor_1 (.a(Register_2__RS2_q), .b(Register_1__RS1_q), .out(adder_1_out[7:0]));  // open: bin, bout
  Multiplexer #(.select(3), .width(32)) multiplexer_1 (
    .in0(adder_1_out), .in1(undriven_2), .in2(undriven), .in3(undriven_3), .in4(undriven_4),
    .in5(undriven_5), .in6(undriven_6), .in7(undriven_7), .out(multiplexer_1_out), .sel(undriven_8),
    .en(undriven_9));
  // Pins of 8 and 32 bits meet at adder_1_out

  // Notes on the sheet:
  //   För hur Subtract ska byggas och kopplas helt, se Logisim subtractor
  //   SLL = Shift Left Logical
endmodule
